# Fritzing sketch BoardDesign (saved by Fritzing 0.7.5b)
breadboards: 1

parts:
  Nano1 = Arduino Nano v2.3
  LCD1 = LCD screen
  S1 = Pushbutton [package="[THT]"]
  S2 = Pushbutton [package="[THT]"]
  R1 = Trimmer Potentiometer [maximum_resistance=10kΩ package=THT]
  R2 = Resistor [tolerance=±5% resistance=4.7k package=THT]
  D1 = Rectifier Diode [part_number=1N4001 package="300 mil [THT]"]
  J2 = Screw terminal - 2 pins [package=THT]
  J3 = Screw terminal - 2 pins [package=THT]
  R3 = Resistor [tolerance=±5% resistance=4.7k package=THT]
  J4 = screw terminal, 4 pins

nets:
  GND: Nano1.GND, LCD1.VSS, LCD1.R/W, LCD1.LED-, S1.Pin_1, S1.Pin_2, S2.Pin_1, S2.Pin_2, R1.leg2, J2.pin1, J3.pin1, J4.pin4
  N1: Nano1.D2, LCD1.DB7
  N2: Nano1.D3, LCD1.DB6
  N3: Nano1.D4, LCD1.DB5
  N4: Nano1.D5, LCD1.DB4
  N5: Nano1.D6, LCD1.E
  N6: Nano1.D7, LCD1.RS
  N7: Nano1.D8, S1.Pin_3, S1.Pin_4
  N8: Nano1.D9, S2.Pin_3, S2.Pin_4
  N9: Nano1.D10, J4.pin3
  N10: Nano1.D11, J3.pin2, R3.Pin_0
  N11: Nano1.D12, R2.Pin_0, J2.pin2
  N12: Nano1.D13, J4.pin2
  +5V: Nano1.+5V, LCD1.VDD, R1.leg1, R2.Pin_1, D1.anode, R3.Pin_1, J4.pin1
  N13: LCD1.V0, R1.wiper
  N14: LCD1.LED+, D1.cathode
